# Fritzing sketch Smart Security System (saved by Fritzing 0.9.3b)
circuit board: 8.46667cm x 5.64444cm
breadboards: 1

parts:
  PIR1 = PIR sensor
  U1 = NodeMCU V1.0

nets:
  VDD: PIR1.VDD, U1.3V3
  N1: PIR1.SIG, U1.D7
  GND: PIR1.GND, U1.GND

custom parts:
  NodeMCU V1.0: ESP8266 based NodeMCU

// code stored in the sketch: Untitled5.ino
#include <ESP8266WiFi.h>
#include <WiFiClientSecure.h>
#include <UniversalTelegramBot.h>
#include <ArduinoJson.h>

// Replace with your network credentials
const char* ssid = "Gearbox Staff";
const char* password = "Staff@Gearbox";

// Initialize Telegram BOT
#define BOTtoken "1721907985:AAG7afgWtHiTr4f3vjmzTmstN3lcvceq6co"  // your Bot Token (Get from Botfather)

// Use @myidbot to find out the chat ID of an individual or a group
// Also note that you need to click "start" on a bot before it can
// message you
#define CHAT_ID "585595092"

WiFiClientSecure client;
UniversalTelegramBot bot(BOTtoken, client);

const int motionSensor = 13; // PIR Motion Sensor
bool motionDetected = false;

// Indicates when motion is detected
void ICACHE_RAM_ATTR detectsMovement() {
  //Serial.println("MOTION DETECTED!!!");
  motionDetected = true;
}

void setup() {
  Serial.begin(115200);
  client.setInsecure();

  // PIR Motion Sensor mode INPUT_PULLUP
  pinMode(motionSensor, INPUT_PULLUP);
  // Set motionSensor pin as interrupt, assign interrupt function and set RISING mode
  attachInterrupt(digitalPinToInterrupt(motionSensor), detectsMovement, RISING);

  // Attempt to connect to Wifi network:
  Serial.print("Connecting Wifi: ");
  Serial.println(ssid);

  WiFi.mode(WIFI_STA);
  WiFi.begin(ssid, password);

  while (WiFi.status() != WL_CONNECTED) {
    Serial.print(".");
    delay(500);
  }

  Serial.println("");
  Serial.println("WiFi connected");
  Serial.print("IP address: ");
  Serial.println(WiFi.localIP());

  bot.sendMessage(CHAT_ID, "Bot started up", "");
}

void loop() {
  if(motionDetected){
    bot.sendMessage(CHAT_ID, "Motion detected!!", "");
    Serial.println("Motion Detected");
    motionDetected = false;
  }
}
